// Logisim project Cache_Optimization.circ as structural Verilog: 14 circuits, main circuit OPTIMIZATION
module OPTIMIZATION (
  input  in_1,
  input  in_2,
  input  in_3,
  input  in_4
);

  wire clk, Data, Hit_Miss, Load, LoadL, not_1_out, not_2_out, not_3_out, not_4_out, not_5_out, not_6_out,
       not_7_out, or_1_out, or_2_out, or_3_out, Store;
  wire [2:0] controlled_buffer_3_out, Rb;
  wire [3:0] ALU_overflow;
  wire [7:0] ALU_y, Cache_and_Memory_data_output, controlled_buffer_1_out, controlled_buffer_6_out,
       Register_Bank_out_a, Register_Bank_out_b;
  wire [15:0] Address, PC_instruction;
  wire [21:0] ram_1_data;
  wire [21:19] IR_q;

  Clock clock_1 (.out(clk));
  CACHE Cache_and_Memory (
    .Address(Address), .Load(Load), .Store(Store), .Clock(clk), .Data(controlled_buffer_6_out),
    .Hit_Miss(Hit_Miss), .Data_Output(Cache_and_Memory_data_output));
  or or_1 (or_1_out, Load, Store);
  assign controlled_buffer_1_out = Load ? Cache_and_Memory_data_output : 8'bz;  // Controlled_Buffer controlled_buffer_1
  Program_Counter PC (
    .Input___Enable(in_2), .Input_Data({16{1'b0}}), .Hit_Miss(Hit_Miss), .Load_Store(or_1_out), .Clock(clk),
    .Instruction(PC_instruction));
  assign controlled_buffer_1_out = LoadL ? Address[7:0] : 8'bz;  // Controlled_Buffer controlled_buffer_2
  assign controlled_buffer_3_out = or_2_out ? Rb : 3'bz;  // Controlled_Buffer controlled_buffer_3
  or or_2 (or_2_out, LoadL, Load);
  assign controlled_buffer_1_out = Data ? ALU_y : 8'bz;  // Controlled_Buffer controlled_buffer_4
  assign controlled_buffer_3_out = Data ? Address[5:3] : 3'bz;  // Controlled_Buffer controlled_buffer_5
  RAM #(.addrWidth(16), .dataWidth(22)) ram_1 (
    .addr(PC_instruction), .data(ram_1_data), .clk(clk), .clr(in_4));  // open: sel, ld
  or or_3 (or_3_out, Data, Load, LoadL);
  Register #(.width(22)) IR (.D(ram_1_data), .Q({IR_q, Address, Rb}), .clk(clk), .clr(in_3));  // open: en
  Register_Bank Register_Bank (
    .Clock(clk), .Write(or_3_out), .Data(controlled_buffer_1_out), .RegSelect(controlled_buffer_3_out),
    .R_A(Address[2:0]), .R_B(Rb), .Out_A(Register_Bank_out_a), .Out_B(Register_Bank_out_b));
  assign controlled_buffer_6_out = Store ? Register_Bank_out_b : 8'bz;  // Controlled_Buffer controlled_buffer_6
  not not_1 (not_1_out, IR_q[21]);
  and and_1 (Data, not_1_out, not_2_out, IR_q[19]);
  not not_2 (not_2_out, IR_q[20]);
  not not_3 (not_3_out, IR_q[21]);
  and and_2 (Load, not_3_out, IR_q[20], not_4_out);
  not not_4 (not_4_out, IR_q[19]);
  not not_5 (not_5_out, IR_q[20]);
  and and_3 (Store, IR_q[21], not_5_out, not_6_out);
  not not_6 (not_6_out, IR_q[19]);
  not not_7 (not_7_out, IR_q[21]);
  and and_4 (LoadL, not_7_out, IR_q[20], IR_q[19]);
  ALU ALU (
    .A(Register_Bank_out_a), .B(Register_Bank_out_b), .opcode(Address[15:12]), .Y(ALU_y),
    .Overflow(ALU_overflow[0]), .Cout(ALU_overflow[1]), .Z(ALU_overflow[2]), .N(ALU_overflow[3]));
  Register #(.width(4)) register_1 (.D(ALU_overflow), .clk(clk), .clr(in_1));  // open: en, Q

  // Other names for the same wires on the sheet: Ra[2:0] = Address[2:0]; Value[7:0] = Address[7:0];
  //   RegSelect[2:0] = Address[5:3]; opcode[3:0] = Address[15:12]

  // Notes on the sheet:
  //   Instruction Memory (ROM/Input)
endmodule

module CACHE (
  input  [15:0] Address,
  input  [7:0] Data,
  input  Load,
  input  Store,
  input  Clock,
  output Hit_Miss,
  output [7:0] Data_Output
);

  wire and_1_out, and_2_out, and_3_out, and_4_out, and_5_out, and_6_out, Cache_Controller_1_regulator_1,
       Cache_Controller_2_regulator_2, MB, not_1_out, not_2_out, not_3_out, not_4_out, not_5_out, not_6_out,
       not_7_out, or_1_out, or_2_out, or_3_out;
  wire [1:0] Tag_Array_specific_bits;
  wire [7:0] Block_Array_data, Memory_data_out, multiplexer_4_out;
  wire [9:0] Cache_Controller_1_block_address, Cache_Controller_2_send_location_to_block_array,
       multiplexer_1_out, multiplexer_2_out, Tag_Array_memory_loc, TO;
  wire [15:0] Cache_Controller_1_memory_address, Cache_Controller_2_send_location_to_main_memory,
       multiplexer_3_out;

  Cache_Controller_1 Cache_Controller_1 (
    .Hit_Miss(Hit_Miss), .Modified_Bit(MB), .Clock(Clock), .Address_Input(Address),
    .Memory_Loc(Tag_Array_memory_loc), .Block_Address(Cache_Controller_1_block_address),
    .Regulator_1(Cache_Controller_1_regulator_1), .Load_Store(or_1_out),
    .Specific_Bits(Tag_Array_specific_bits), .Memory_Address(Cache_Controller_1_memory_address));
  Tag_Array Tag_Array (
    .Clock(Clock), .Address(Address), .Regulator_2(Cache_Controller_2_regulator_2),
    .Regulator_1(Cache_Controller_1_regulator_1), .Modified_Bit(MB), .Memory_Loc(Tag_Array_memory_loc),
    .Store(Store), .Load(Load), .Hit_Miss(Hit_Miss), .Tag_Output(TO), .Specific_Bits(Tag_Array_specific_bits));
  or or_1 (or_1_out, Load, Store);
  Cache_Controller_2 Cache_Controller_2 (
    .Send_Location_To_Main_Memory(Cache_Controller_2_send_location_to_main_memory),
    .Send_Location_To_Block_Array(Cache_Controller_2_send_location_to_block_array),
    .Receive_Address(Address), .Receive_Specific_Bits(Tag_Array_specific_bits), .Modified_Bit(MB),
    .Hit_Miss(Hit_Miss), .Clock(Clock), .Regulator_2(Cache_Controller_2_regulator_2), .Load_Store(or_1_out));
  and and_1 (and_1_out, Store, Hit_Miss);
  Multiplexer #(.width(10)) multiplexer_1 (
    .in0(Cache_Controller_2_send_location_to_block_array), .in1(Cache_Controller_1_block_address),
    .out(multiplexer_1_out), .sel(MB));  // open: en
  or or_2 (or_2_out, and_1_out, and_2_out);
  and and_2 (and_2_out, not_1_out, not_2_out);
  not not_1 (not_1_out, Hit_Miss);
  not not_2 (not_2_out, MB);
  Multiplexer #(.width(10)) multiplexer_2 (
    .in0(multiplexer_1_out), .in1(TO), .out(multiplexer_2_out), .sel(Hit_Miss));  // open: en
  Block_Array Block_Array (
    .Location(multiplexer_2_out), .Write_Data(multiplexer_4_out), .Clock(Clock), .Store(or_2_out),
    .Load(or_3_out), .Data(Block_Array_data));  // open: Enable
  or or_3 (or_3_out, and_3_out, and_4_out);
  not not_3 (not_3_out, Hit_Miss);
  and and_3 (and_3_out, Load, Hit_Miss);
  and and_4 (and_4_out, not_3_out, MB);
  not not_4 (not_4_out, Hit_Miss);
  Multiplexer #(.width(16)) multiplexer_3 (
    .in0(Cache_Controller_2_send_location_to_main_memory), .in1(Cache_Controller_1_memory_address),
    .out(multiplexer_3_out), .sel(MB), .en(not_4_out));
  not not_5 (not_5_out, Hit_Miss);
  Memory Memory (
    .Location(multiplexer_3_out), .Write_Data(Block_Array_data), .Store(and_5_out), .Clock(Clock),
    .Load(and_6_out), .Data_Out(Memory_data_out));  // open: Enable
  and and_5 (and_5_out, not_5_out, MB);
  and and_6 (and_6_out, not_6_out, not_7_out);
  not not_6 (not_6_out, Hit_Miss);
  Multiplexer #(.width(8)) multiplexer_4 (
    .in0(Memory_data_out), .in1(Data), .out(multiplexer_4_out), .sel(Hit_Miss));  // open: en
  not not_7 (not_7_out, MB);
  assign Data_Output = Hit_Miss ? Block_Array_data : 8'bz;  // Controlled_Buffer controlled_buffer_1

  // Other names for the same wires on the sheet: Hit = Hit_Miss
endmodule

module Tag_Array (
  input  Clock,
  input  [15:0] Address,
  input  Store,
  input  Load,
  input  Regulator_2,
  input  Regulator_1,
  output Hit_Miss,
  output Modified_Bit,
  output [9:0] Memory_Loc,
  output [9:0] Tag_Output,
  output [1:0] Specific_Bits
);

  wire and_6_out, and_7_out, and_8_out, and_9_out, comparator_1_eq, comparator_2_eq, comparator_3_eq,
       comparator_4_eq, decoder_1_out0, decoder_1_out1, decoder_1_out2, decoder_1_out3, load_store,
       not_1_out, or_1_out, or_3_out, priority_encoder_1_p2, priority_encoder_1_p3, priority_encoder_1_p4,
       priority_encoder_1_p5, priority_encoder_1_p6, R1, R2, R3, R4, Ram_1, Ram_2, Ram_3, Ram_4, Store_1,
       Store_2, Store_3, Store_4;
  wire [1:0] lru_1_ram_no, priority_encoder_1_p1;
  wire [9:0] Data_1, Data_2, Data_3, Data_4, Input_1, Input_2, Input_3, Input_4, multiplexer_1_out, Tag_1,
       Tag_2, Tag_3, Tag_4;

  Multiplexer #(.width(10)) multiplexer_1 (
    .in0({2'b10, Address[15:8]}), .in1({10{1'b0}}), .out(multiplexer_1_out), .sel(Regulator_1));  // open: en
  or or_1 (or_1_out, Regulator_2, Regulator_1);
  Decoder #(.select(2), .disabled(0)) decoder_1 (
    .out0(decoder_1_out0), .out1(decoder_1_out1), .out2(decoder_1_out2), .out3(decoder_1_out3),
    .sel(Specific_Bits), .en(or_1_out));
  Multiplexer #(.width(10)) multiplexer_2 (
    .in0(Data_1), .in1(multiplexer_1_out), .out(Input_1), .sel(decoder_1_out0));  // open: en
  or or_2 (load_store, Store, Load);
  not not_1 (not_1_out, Hit_Miss);
  Multiplexer #(.width(10)) multiplexer_3 (
    .in0(Data_2), .in1(multiplexer_1_out), .out(Input_2), .sel(decoder_1_out1));  // open: en
  // Priority_Encoder #(.select(2)) priority_encoder_1: pin names not known; wires that end beside it: priority_encoder_1_p1, priority_encoder_1_p2, priority_encoder_1_p3, priority_encoder_1_p4, priority_encoder_1_p5, priority_encoder_1_p6
  and and_1 (priority_encoder_1_p2, not_1_out, or_3_out);
  RAM #(.addrWidth(5), .dataWidth(10), .bus("separate")) u_ram_1 (
    .addr(Address[7:3]), .din(Input_1), .data(Tag_1), .str(Store_1), .sel(load_store), .clk(Clock), .ld(1'b1));  // open: clr
  RAM #(.addrWidth(5), .dataWidth(10), .bus("separate")) u_ram_2 (
    .addr(Address[7:3]), .din(Input_2), .data(Tag_2), .str(Store_2), .sel(load_store), .clk(Clock), .ld(1'b1));  // open: clr
  RAM #(.addrWidth(5), .dataWidth(10), .bus("separate")) u_ram_3 (
    .addr(Address[7:3]), .din(Input_3), .data(Tag_3), .str(Store_3), .sel(load_store), .clk(Clock), .ld(1'b1));  // open: clr
  RAM #(.addrWidth(5), .dataWidth(10), .bus("separate")) u_ram_4 (
    .addr(Address[7:3]), .din(Input_4), .data(Tag_4), .str(Store_4), .sel(load_store), .clk(Clock), .ld(1'b1));  // open: clr
  Multiplexer #(.width(10)) multiplexer_4 (
    .in0(Data_3), .in1(multiplexer_1_out), .out(Input_3), .sel(decoder_1_out2));  // open: en
  not not_2 (priority_encoder_1_p3, Tag_1[9]);
  not not_3 (priority_encoder_1_p5, Tag_3[9]);
  not not_4 (priority_encoder_1_p6, Tag_4[9]);
  not not_5 (priority_encoder_1_p4, Tag_2[9]);
  or or_3 (or_3_out, priority_encoder_1_p3, priority_encoder_1_p4, priority_encoder_1_p5, priority_encoder_1_p6);
  Multiplexer #(.width(10)) multiplexer_5 (
    .in0(Data_4), .in1(multiplexer_1_out), .out(Input_4), .sel(decoder_1_out3));  // open: en
  Comparator #(.mode("unsigned")) comparator_1 (
    .a(Tag_1[7:0]), .b(Address[15:8]), .eq(comparator_1_eq));  // open: gt, lt
  and and_2 (R1, comparator_1_eq, Tag_1[9]);
  Comparator #(.mode("unsigned")) comparator_2 (
    .a(Tag_2[7:0]), .b(Address[15:8]), .eq(comparator_2_eq));  // open: gt, lt
  and and_3 (R2, comparator_2_eq, Tag_2[9]);
  Comparator #(.mode("unsigned")) comparator_3 (
    .a(Tag_3[7:0]), .b(Address[15:8]), .eq(comparator_3_eq));  // open: gt, lt
  and and_4 (R3, comparator_3_eq, Tag_3[9]);
  Comparator #(.mode("unsigned")) comparator_4 (
    .a(Tag_4[7:0]), .b(Address[15:8]), .eq(comparator_4_eq));  // open: gt, lt
  and and_5 (R4, comparator_4_eq, Tag_4[9]);
  or u_Hit_Miss (Hit_Miss, R1, R2, R3, R4);
  and and_6 (and_6_out, Store, Ram_1);
  or or_4 (Store_1, and_6_out, decoder_1_out0);
  and and_7 (and_7_out, Store, Ram_2);
  or or_5 (Store_2, and_7_out, decoder_1_out1);
  assign Data_1 = {1'b0, R1, {8{1'b0}}} | Tag_1;  // OR_Gate or_6, 10 bits wide
  assign Data_2 = {1'b0, R2, {8{1'b0}}} | Tag_2;  // OR_Gate or_7, 10 bits wide
  or or_8 (Tag_Output[3], R2, R4);
  or or_9 (Tag_Output[4], R3, R4);
  assign Data_3 = {1'b0, R3, {8{1'b0}}} | Tag_3;  // OR_Gate or_10, 10 bits wide
  assign Data_4 = {1'b0, R4, {8{1'b0}}} | Tag_4;  // OR_Gate or_11, 10 bits wide
  and and_8 (and_8_out, Store, Ram_3);
  or or_12 (Store_3, and_8_out, decoder_1_out2);
  and and_9 (and_9_out, Store, Ram_4);
  or or_13 (Store_4, and_9_out, decoder_1_out3);
  Decoder #(.select(2), .disabled(0)) decoder_2 (
    .out0(Ram_1), .out1(Ram_2), .out2(Ram_3), .out3(Ram_4), .sel(Tag_Output[4:3]), .en(Store));
  Multiplexer #(.width(2)) multiplexer_6 (
    .in0(lru_1_ram_no), .in1(priority_encoder_1_p1), .out(Specific_Bits), .sel(or_3_out));  // open: en
  Multiplexer #(.select(2)) multiplexer_7 (
    .in0(Tag_1[8]), .in1(Tag_2[8]), .in2(Tag_3[8]), .in3(Tag_4[8]), .out(Modified_Bit), .sel(Specific_Bits));  // open: en
  Multiplexer #(.select(2), .width(10)) multiplexer_8 (
    .in0(Tag_1), .in1(Tag_2), .in2(Tag_3), .in3(Tag_4), .out(Memory_Loc), .sel(Specific_Bits));  // open: en
  LRU lru_1 (
    .Clock(Clock), .Address(Address[7:3]), .load_store(load_store), .Hit_Miss(Hit_Miss), .R1(R1), .R2(R2),
    .R3(R3), .R4(R4), .RAM_No(lru_1_ram_no));

  assign {Tag_Output[9:5], Tag_Output[2:0]} = Address[7:0];

  // Other names for the same wires on the sheet: clk = Clock; DATA[7:0] = Address[15:8]; Tag[7:0] = Address[15:8];
  //   Index[4:0] = Address[7:3]

  // Notes on the sheet:
  //   RAM 1
  //   RAM 2
  //   RAM 3
  //   RAM 4
endmodule

module LRU (
  input  Clock,
  input  [4:0] Address,
  input  Hit_Miss,
  input  R1,
  input  load_store,
  input  R2,
  input  R3,
  input  R4,
  output [1:0] RAM_No
);

  wire comparator_1_eq, comparator_2_eq, comparator_3_eq, comparator_4_eq, comparator_5_gt, comparator_6_gt;
  wire [2:0] D1, D2, D3, D4, multiplexer_1_out, multiplexer_2_out, multiplexer_3_out, multiplexer_4_out,
       multiplexer_5_out, multiplexer_6_out, multiplexer_7_out, multiplexer_8_out, multiplexer_9_out,
       multiplexer_10_out, subtractor_1_out, subtractor_2_out, subtractor_3_out, subtractor_4_out;

  Multiplexer #(.width(3)) multiplexer_1 (
    .in0(multiplexer_5_out), .in1(3'b111), .out(multiplexer_1_out), .sel(R1));  // open: en
  Multiplexer #(.width(3)) multiplexer_2 (
    .in0(multiplexer_6_out), .in1(3'b111), .out(multiplexer_2_out), .sel(R2));  // open: en
  Multiplexer #(.width(3)) multiplexer_3 (
    .in0(multiplexer_7_out), .in1(3'b111), .out(multiplexer_3_out), .sel(R3));  // open: en
  Multiplexer #(.width(3)) multiplexer_4 (
    .in0(multiplexer_8_out), .in1(3'b111), .out(multiplexer_4_out), .sel(R4));  // open: en
  RAM #(.addrWidth(5), .dataWidth(3), .bus("separate")) ram_1 (
    .addr(Address), .din(multiplexer_1_out), .data(D1), .str(Hit_Miss), .sel(load_store), .clk(Clock),
    .ld(1'b1));  // open: clr
  RAM #(.addrWidth(5), .dataWidth(3), .bus("separate")) ram_2 (
    .addr(Address), .din(multiplexer_2_out), .data(D2), .str(Hit_Miss), .sel(load_store), .clk(Clock),
    .ld(1'b1));  // open: clr
  RAM #(.addrWidth(5), .dataWidth(3), .bus("separate")) ram_3 (
    .addr(Address), .din(multiplexer_3_out), .data(D3), .str(Hit_Miss), .sel(load_store), .clk(Clock),
    .ld(1'b1));  // open: clr
  RAM #(.addrWidth(5), .dataWidth(3), .bus("separate")) ram_4 (
    .addr(Address), .din(multiplexer_4_out), .data(D4), .str(Hit_Miss), .sel(load_store), .clk(Clock),
    .ld(1'b1));  // open: clr
  Subtractor #(.width(3)) subtractor_1 (.a(D1), .b(3'b001), .out(subtractor_1_out));  // open: bin, bout
  Comparator #(.width(3), .mode("unsigned")) comparator_1 (.a(D1), .b(3'b000), .eq(comparator_1_eq));  // open: gt, lt
  Subtractor #(.width(3)) subtractor_2 (.a(D2), .b(3'b001), .out(subtractor_2_out));  // open: bin, bout
  Comparator #(.width(3), .mode("unsigned")) comparator_2 (.a(D2), .b(3'b000), .eq(comparator_2_eq));  // open: gt, lt
  Subtractor #(.width(3)) subtractor_3 (.a(D3), .b(3'b001), .out(subtractor_3_out));  // open: bin, bout
  Comparator #(.width(3), .mode("unsigned")) comparator_3 (.a(D3), .b(3'b000), .eq(comparator_3_eq));  // open: gt, lt
  Subtractor #(.width(3)) subtractor_4 (.a(D4), .b(3'b001), .out(subtractor_4_out));  // open: bin, bout
  Comparator #(.width(3), .mode("unsigned")) comparator_4 (.a(D4), .b(3'b000), .eq(comparator_4_eq));  // open: gt, lt
  Multiplexer #(.width(3)) multiplexer_5 (
    .in0(subtractor_1_out), .in1(3'b000), .out(multiplexer_5_out), .sel(comparator_1_eq));  // open: en
  Multiplexer #(.width(3)) multiplexer_6 (
    .in0(subtractor_2_out), .in1(3'b000), .out(multiplexer_6_out), .sel(comparator_2_eq));  // open: en
  Multiplexer #(.width(3)) multiplexer_7 (
    .in0(subtractor_3_out), .in1(3'b000), .out(multiplexer_7_out), .sel(comparator_3_eq));  // open: en
  Multiplexer #(.width(3)) multiplexer_8 (
    .in0(subtractor_4_out), .in1(3'b000), .out(multiplexer_8_out), .sel(comparator_4_eq));  // open: en
  Comparator #(.width(3), .mode("unsigned")) comparator_5 (.a(D1), .b(D2), .gt(comparator_5_gt));  // open: eq, lt
  Comparator #(.width(3), .mode("unsigned")) comparator_6 (.a(D3), .b(D4), .gt(comparator_6_gt));  // open: eq, lt
  Multiplexer #(.width(3)) multiplexer_9 (
    .in0(D1), .in1(D2), .out(multiplexer_9_out), .sel(comparator_5_gt));  // open: en
  Multiplexer #(.width(3)) multiplexer_10 (
    .in0(D3), .in1(D4), .out(multiplexer_10_out), .sel(comparator_6_gt));  // open: en
  Comparator #(.width(3), .mode("unsigned")) comparator_7 (
    .a(multiplexer_9_out), .b(multiplexer_10_out), .gt(RAM_No[1]));  // open: eq, lt
  Multiplexer multiplexer_11 (
    .in0(comparator_5_gt), .in1(comparator_6_gt), .out(RAM_No[0]), .sel(RAM_No[1]));  // open: en

  // Other names for the same wires on the sheet: Clk = Clock

  // Notes on the sheet:
  //   LRU 1
  //   LRU 2
  //   LRU 3
  //   LRU 4
endmodule

module Block_Array (
  input  [9:0] Location,
  input  [7:0] Write_Data,
  input  Enable,
  input  Clock,
  input  Store,
  input  Load,
  output [7:0] Data
);

  RAM #(.addrWidth(10), .bus("separate")) ram_1 (
    .addr(Location), .din(Write_Data), .data(Data), .str(Store), .sel(Enable), .clk(Clock), .ld(Load));  // open: clr

  // Notes on the sheet:
  //   Block Array
endmodule

module Memory (
  input  [15:0] Location,
  input  [7:0] Write_Data,
  input  Clock,
  input  Store,
  input  Load,
  input  Enable,
  output [7:0] Data_Out
);

  RAM #(.addrWidth(16), .bus("separate")) ram_1 (
    .addr(Location), .din(Write_Data), .data(Data_Out), .str(Store), .sel(Enable), .clk(Clock), .ld(Load));  // open: clr
endmodule

module Cache_Controller_1 (
  input  Hit_Miss,
  input  Modified_Bit,
  input  Clock,
  input  [1:0] Specific_Bits,
  input  [15:0] Address_Input,
  input  [9:0] Memory_Loc,
  input  Load_Store,
  output [9:0] Block_Address,
  output [15:0] Memory_Address,
  output Regulator_1
);

  wire and_1_out, multiplexer_1_out, not_1_out;

  not not_1 (not_1_out, Hit_Miss);
  and and_1 (and_1_out, not_1_out, Modified_Bit);
  Multiplexer multiplexer_1 (.in0(1'b1), .in1(1'b0), .out(multiplexer_1_out), .sel(Load_Store));  // open: en
  Counter #(.width(3), .max('h7)) counter_1 (
    .count(and_1_out), .Q(Block_Address[2:0]), .carry(Regulator_1), .clk(Clock), .clr(multiplexer_1_out));  // open: load, D

  assign Block_Address[9:3] = {Address_Input[7:3], Specific_Bits};
  assign Memory_Address = {Memory_Loc[7:0], Address_Input[7:3], Block_Address[2:0]};
endmodule

module Cache_Controller_2 (
  input  [1:0] Receive_Specific_Bits,
  input  Clock,
  input  [15:0] Receive_Address,
  input  Hit_Miss,
  input  Modified_Bit,
  input  Load_Store,
  output [9:0] Send_Location_To_Block_Array,
  output [15:0] Send_Location_To_Main_Memory,
  output Regulator_2
);

  wire and_1_out, multiplexer_1_out, not_1_out, not_2_out;

  not not_1 (not_1_out, Modified_Bit);
  Counter #(.width(3), .max('h7)) counter_1 (
    .count(and_1_out), .Q(Send_Location_To_Block_Array[2:0]), .carry(Regulator_2), .clk(Clock),
    .clr(multiplexer_1_out));  // open: load, D
  and and_1 (and_1_out, not_1_out, not_2_out);
  not not_2 (not_2_out, Hit_Miss);
  Multiplexer multiplexer_1 (.in0(1'b1), .in1(1'b0), .out(multiplexer_1_out), .sel(Load_Store));  // open: en

  assign Send_Location_To_Block_Array[9:3] = {Receive_Address[7:3], Receive_Specific_Bits};
  assign Send_Location_To_Main_Memory = {Receive_Address[15:3], Send_Location_To_Block_Array[2:0]};
endmodule

module ALU (
  input  [7:0] A,
  input  [7:0] B,
  input  [3:0] opcode,
  output [7:0] Y,
  output Overflow,
  output Cout,
  output Z,
  output N
);

  wire [7:0] arithmetic_unit_1_sum, logic_unit_1_y, multiplexer_1_out, multiplexer_2_out, not_1_out,
       not_2_out;

  assign not_1_out = ~A;  // NOT_Gate not_1, 8 bits wide
  assign not_2_out = ~B;  // NOT_Gate not_2, 8 bits wide
  Multiplexer #(.width(8), .enable("false")) multiplexer_1 (
    .in0(A), .in1(not_1_out), .out(multiplexer_1_out), .sel(opcode[0]));
  Multiplexer #(.width(8), .enable("false")) multiplexer_2 (
    .in0(B), .in1(not_2_out), .out(multiplexer_2_out), .sel(opcode[1]));
  Arithmetic_Unit arithmetic_unit_1 (
    .Cin(opcode[2]), .A(multiplexer_1_out), .B(multiplexer_2_out), .Sum(arithmetic_unit_1_sum),
    .Overflow(Overflow), .Cout(Cout));
  Logic_Unit logic_unit_1 (.A(A), .B(multiplexer_2_out), .s1(opcode[0]), .s2(opcode[2]), .Y(logic_unit_1_y));
  Multiplexer #(.width(8), .enable("false")) multiplexer_3 (
    .in0(arithmetic_unit_1_sum), .in1(logic_unit_1_y), .out({N, Y[6:0]}), .sel(opcode[3]));
  nor nor_1 (Z, Y[0], Y[1], Y[2], Y[3], Y[4], Y[5], Y[6], N);

  assign Y[7] = N;
endmodule

module Register_Bank (
  input  Clock,
  input  Write,
  input  [7:0] Data,
  input  [2:0] R_A,
  input  [2:0] RegSelect,
  input  [2:0] R_B,
  output [7:0] Out_A,
  output [7:0] Out_B
);

  wire demultiplexer_1_out0, demultiplexer_1_out1, demultiplexer_1_out2, demultiplexer_1_out3,
       demultiplexer_1_out4, demultiplexer_1_out5, demultiplexer_1_out6, demultiplexer_1_out7;
  wire [7:0] R0_q, R1_q, R2_q, R3_q, R4_q, R5_q, R6_q, R7_q;

  Demultiplexer #(.select(3), .enable("false")) demultiplexer_1 (
    .out0(demultiplexer_1_out0), .out1(demultiplexer_1_out1), .out2(demultiplexer_1_out2),
    .out3(demultiplexer_1_out3), .out4(demultiplexer_1_out4), .out5(demultiplexer_1_out5),
    .out6(demultiplexer_1_out6), .out7(demultiplexer_1_out7), .in(Write), .sel(RegSelect));
  Register R0 (.D(Data), .en(demultiplexer_1_out0), .Q(R0_q), .clk(Clock), .clr(1'b0));
  Register R1 (.D(Data), .en(demultiplexer_1_out1), .Q(R1_q), .clk(Clock), .clr(1'b0));
  Register R2 (.D(Data), .en(demultiplexer_1_out2), .Q(R2_q), .clk(Clock), .clr(1'b0));
  Register R3 (.D(Data), .en(demultiplexer_1_out3), .Q(R3_q), .clk(Clock), .clr(1'b0));
  Register R4 (.D(Data), .en(demultiplexer_1_out4), .Q(R4_q), .clk(Clock), .clr(1'b0));
  Register R5 (.D(Data), .en(demultiplexer_1_out5), .Q(R5_q), .clk(Clock), .clr(1'b0));
  Register R6 (.D(Data), .en(demultiplexer_1_out6), .Q(R6_q), .clk(Clock), .clr(1'b0));
  Register R7 (.D(Data), .en(demultiplexer_1_out7), .Q(R7_q), .clk(Clock), .clr(1'b0));
  Multiplexer #(.select(3), .width(8), .enable("false")) multiplexer_1 (
    .in0(R0_q), .in1(R1_q), .in2(R2_q), .in3(R3_q), .in4(R4_q), .in5(R5_q), .in6(R6_q), .in7(R7_q),
    .out(Out_A), .sel(R_A));
  Multiplexer #(.select(3), .width(8), .enable("false")) multiplexer_2 (
    .in0(R0_q), .in1(R1_q), .in2(R2_q), .in3(R3_q), .in4(R4_q), .in5(R5_q), .in6(R6_q), .in7(R7_q),
    .out(Out_B), .sel(R_B));
endmodule

// AU
module Arithmetic_Unit (
  input  Cin,
  input  [7:0] A,
  input  [7:0] B,
  output [7:0] Sum,
  output Overflow,
  output Cout
);

  wire adder_1_cout, adder_2_cout, adder_3_cout, adder_4_cout, adder_5_cout, adder_6_cout, adder_7_cout;

  Adder #(.width(1)) adder_1 (.a(A[0]), .b(B[0]), .out(Sum[0]), .cin(Cin), .cout(adder_1_cout));
  Adder #(.width(1)) adder_2 (.a(A[1]), .b(B[1]), .out(Sum[1]), .cin(adder_1_cout), .cout(adder_2_cout));
  Adder #(.width(1)) adder_3 (.a(A[2]), .b(B[2]), .out(Sum[2]), .cin(adder_2_cout), .cout(adder_3_cout));
  Adder #(.width(1)) adder_4 (.a(A[3]), .b(B[3]), .out(Sum[3]), .cin(adder_3_cout), .cout(adder_4_cout));
  Adder #(.width(1)) adder_5 (.a(A[4]), .b(B[4]), .out(Sum[4]), .cin(adder_4_cout), .cout(adder_5_cout));
  Adder #(.width(1)) adder_6 (.a(A[5]), .b(B[5]), .out(Sum[5]), .cin(adder_5_cout), .cout(adder_6_cout));
  Adder #(.width(1)) adder_7 (.a(A[6]), .b(B[6]), .out(Sum[6]), .cin(adder_6_cout), .cout(adder_7_cout));
  Adder #(.width(1)) adder_8 (.a(A[7]), .b(B[7]), .out(Sum[7]), .cin(adder_7_cout), .cout(Cout));
  xor xor_1 (Overflow, adder_7_cout, Cout);
endmodule

// LU
module Logic_Unit (
  input  [7:0] A,
  input  [7:0] B,
  input  s1,
  input  s2,
  output [7:0] Y
);

  wire [7:0] and_1_out, or_1_out, xor_1_out;

  assign and_1_out = A & B;  // AND_Gate and_1, 8 bits wide
  assign or_1_out = A | B;  // OR_Gate or_1, 8 bits wide
  assign xor_1_out = A ^ B;  // XOR_Gate xor_1, 8 bits wide
  Multiplexer #(.select(2), .width(8), .enable("false")) multiplexer_1 (
    .in0(and_1_out), .in1(or_1_out), .in2(xor_1_out), .in3(B), .out(Y), .sel({s1, s2}));
endmodule

// PC
module Program_Counter (
  input  Input___Enable,
  input  [15:0] Input_Data,
  input  Hit_Miss,
  input  Load_Store,
  input  Clock,
  output [15:0] Instruction
);

  wire and_1_out, not_1_out, not_2_out, or_1_out;
  wire [15:0] adder_1_out, controlled_buffer_1_out, controlled_buffer_2_out;

  assign controlled_buffer_1_out = Input___Enable ? Input_Data : 16'bz;  // Controlled_Buffer controlled_buffer_1
  and and_1 (and_1_out, Hit_Miss, Load_Store);
  not not_1 (not_1_out, Load_Store);
  not not_2 (not_2_out, Input___Enable);
  or or_1 (or_1_out, and_1_out, not_1_out);
  assign controlled_buffer_2_out = or_1_out ? controlled_buffer_1_out : 16'bz;  // Controlled_Buffer controlled_buffer_2
  assign controlled_buffer_1_out = not_2_out ? adder_1_out : 16'bz;  // Controlled_Buffer controlled_buffer_3
  Register #(.width(16)) register_1 (.D(controlled_buffer_2_out), .Q(Instruction), .clk(Clock));  // open: en, clr
  Adder #(.width(16)) adder_1 (.a(Instruction), .b(16'h1), .out(adder_1_out));  // open: cin, cout
endmodule

module BASELINE (
  input  in_1,
  input  in_2,
  input  in_3,
  input  in_4
);

  wire clk, d_ff_1_q, d_ff_1_qn, d_ff_2_q, d_ff_3_q, d_ff_3_qn, d_ff_4_q, d_ff_4_qn, d_ff_5_qn, d_ff_6_q,
       d_ff_6_qn, Data, Load, LoadL, LoadRdy, not_1_out, not_2_out, not_3_out, not_4_out, not_5_out,
       not_6_out, not_7_out, not_8_out, or_1_out, or_2_out, or_3_out, Store;
  wire [2:0] controlled_buffer_3_out, Rb;
  wire [3:0] ALU_overflow;
  wire [7:0] ALU_y, controlled_buffer_1_out, controlled_buffer_6_out, Memory_data_out, Register_Bank_out_a,
       Register_Bank_out_b;
  wire [15:0] Address, PC_instruction;
  wire [21:0] ram_1_data;
  wire [21:19] IR_q;

  Memory Memory (
    .Location(Address), .Write_Data(controlled_buffer_6_out), .Store(Store), .Clock(clk), .Load(Load),
    .Data_Out(Memory_data_out));  // open: Enable
  Clock clock_1 (.out(clk));
  D_Flip_Flop d_ff_1 (.clk(clk), .D(d_ff_1_qn), .Q(d_ff_1_q), .Qn(d_ff_1_qn));  // open: preset, en, reset
  assign controlled_buffer_1_out = Load ? Memory_data_out : 8'bz;  // Controlled_Buffer controlled_buffer_1
  D_Flip_Flop #(.trigger("high")) d_ff_2 (.clk(clk), .D(LoadRdy), .Q(d_ff_2_q));  // open: Qn, preset, en, reset
  not not_1 (not_1_out, clk);
  or or_1 (or_1_out, Load, Store);
  D_Flip_Flop d_ff_3 (.clk(d_ff_1_q), .D(d_ff_3_qn), .Q(d_ff_3_q), .Qn(d_ff_3_qn));  // open: preset, en, reset
  D_Flip_Flop d_ff_4 (.clk(not_1_out), .D(d_ff_4_qn), .Q(d_ff_4_q), .Qn(d_ff_4_qn));  // open: preset, en, reset
  Program_Counter PC (
    .Input___Enable(in_2), .Input_Data({16{1'b0}}), .Hit_Miss(d_ff_2_q), .Load_Store(or_1_out), .Clock(clk),
    .Instruction(PC_instruction));
  D_Flip_Flop d_ff_5 (
    .clk(d_ff_3_q), .D(d_ff_5_qn), .Q(LoadRdy), .Qn(d_ff_5_qn), .reset(d_ff_6_q));  // open: preset, en
  D_Flip_Flop d_ff_6 (.clk(d_ff_4_q), .D(d_ff_6_qn), .Q(d_ff_6_q), .Qn(d_ff_6_qn));  // open: preset, en, reset
  assign controlled_buffer_1_out = LoadL ? Address[7:0] : 8'bz;  // Controlled_Buffer controlled_buffer_2
  assign controlled_buffer_3_out = or_2_out ? Rb : 3'bz;  // Controlled_Buffer controlled_buffer_3
  or or_2 (or_2_out, LoadL, Load);
  assign controlled_buffer_1_out = Data ? ALU_y : 8'bz;  // Controlled_Buffer controlled_buffer_4
  assign controlled_buffer_3_out = Data ? Address[5:3] : 3'bz;  // Controlled_Buffer controlled_buffer_5
  RAM #(.addrWidth(16), .dataWidth(22)) ram_1 (
    .addr(PC_instruction), .data(ram_1_data), .clk(clk), .clr(in_4));  // open: sel, ld
  or or_3 (or_3_out, Data, Load, LoadL);
  Register #(.width(22)) IR (.D(ram_1_data), .Q({IR_q, Address, Rb}), .clk(clk), .clr(in_3));  // open: en
  Register_Bank Register_Bank (
    .Clock(clk), .Write(or_3_out), .Data(controlled_buffer_1_out), .RegSelect(controlled_buffer_3_out),
    .R_A(Address[2:0]), .R_B(Rb), .Out_A(Register_Bank_out_a), .Out_B(Register_Bank_out_b));
  assign controlled_buffer_6_out = Store ? Register_Bank_out_b : 8'bz;  // Controlled_Buffer controlled_buffer_6
  not not_2 (not_2_out, IR_q[21]);
  and and_1 (Data, not_2_out, not_3_out, IR_q[19]);
  not not_3 (not_3_out, IR_q[20]);
  not not_4 (not_4_out, IR_q[21]);
  and and_2 (Load, not_4_out, IR_q[20], not_5_out);
  not not_5 (not_5_out, IR_q[19]);
  not not_6 (not_6_out, IR_q[20]);
  and and_3 (Store, IR_q[21], not_6_out, not_7_out);
  not not_7 (not_7_out, IR_q[19]);
  not not_8 (not_8_out, IR_q[21]);
  and and_4 (LoadL, not_8_out, IR_q[20], IR_q[19]);
  ALU ALU (
    .A(Register_Bank_out_a), .B(Register_Bank_out_b), .opcode(Address[15:12]), .Y(ALU_y),
    .Overflow(ALU_overflow[0]), .Cout(ALU_overflow[1]), .Z(ALU_overflow[2]), .N(ALU_overflow[3]));
  Register #(.width(4)) register_1 (.D(ALU_overflow), .clk(clk), .clr(in_1));  // open: en, Q

  // Other names for the same wires on the sheet: Ra[2:0] = Address[2:0]; Value[7:0] = Address[7:0];
  //   RegSelect[2:0] = Address[5:3]; opcode[3:0] = Address[15:12]

  // Notes on the sheet:
  //   Instruction Memory (ROM/Input)
endmodule
